// Logisim project Machine.circ as structural Verilog: 2 circuits, main circuit main
module main (
);

  wire Clk_Button_out, CPU_1_p6, CPU_1_p7, CPU_1_p8, CPU_1_p9, CPU_1_p10, CPU_1_p11, CPU_1_p12, CPU_1_p16,
       Rst_Button_out;
  wire [7:0] RAM_Addr, ROM_Addr;
  wire [15:0] ROMa_data;
  wire [31:0] CPU_1_p5, CPU_1_p15, RAMa_dout;
  wire [31:8] CPU_1_p14;

  RAM #(.dataWidth(32), .databus("bibus")) RAMa (
    .addr(RAM_Addr), .we(CPU_1_p16), .oe(1'b1), .clk(Clk_Button_out), .din(CPU_1_p15), .dout(RAMa_dout));
  LED A0 (.in(RAMa_dout[0]));
  LED A1 (.in(RAMa_dout[1]));
  LED A2 (.in(RAMa_dout[2]));
  ROM #(.dataWidth(16)) ROMa (.addr(ROM_Addr), .data(ROMa_data));
  Button Clk_Button (.out(Clk_Button_out));
  Button Rst_Button (.out(Rst_Button_out));
  LED A3 (.in(RAMa_dout[3]));
  LED A4 (.in(RAMa_dout[4]));
  LED A5 (.in(RAMa_dout[5]));
  LED A6 (.in(RAMa_dout[6]));
  LED A7 (.in(RAMa_dout[7]));
  LED L0 (.in(CPU_1_p5[0]));
  // Probe on CPU_1_p6
  // Probe on CPU_1_p5
  LED L3 (.in(CPU_1_p5[3]));
  LED L1 (.in(CPU_1_p5[1]));
  LED L2 (.in(CPU_1_p5[2]));
  // Probe on CPU_1_p8
  // Probe on CPU_1_p7
  // Probe on CPU_1_p10
  // Probe on CPU_1_p9
  LED L4 (.in(CPU_1_p5[4]));
  LED L5 (.in(CPU_1_p5[5]));
  // Probe on CPU_1_p12
  // Probe on CPU_1_p11
  // CPU CPU_1: pin names not known; wires that end beside it: Clk_Button_out, Rst_Button_out, RAMa_dout, ROMa_data, CPU_1_p5, CPU_1_p6, CPU_1_p7, CPU_1_p8, CPU_1_p9, CPU_1_p10, CPU_1_p11, CPU_1_p12, ROM_Addr, {CPU_1_p14, RAM_Addr}, CPU_1_p15, CPU_1_p16
  LED L6 (.in(CPU_1_p5[6]));
  LED L7 (.in(CPU_1_p5[7]));
  LED LED_1 (.in(RAM_Addr[0]));
  LED LED_2 (.in(RAM_Addr[1]));
  LED LED_3 (.in(RAM_Addr[2]));
  LED LED_4 (.in(RAM_Addr[3]));
  LED LED_5 (.in(RAM_Addr[4]));
  LED LED_6 (.in(RAM_Addr[5]));
  LED LED_7 (.in(RAM_Addr[6]));
  LED LED_8 (.in(RAM_Addr[7]));

  // Notes on the sheet:
  //   contents of ROMa (hex, n*v repeats v):
  //   b090 2005 900c 2002 980c 9008 9808 2003 9004 9804 2004 9000 9804
  //   Use only 8 bit adresses
endmodule

module CPU (
  input  [31:0] RAM_In,
  input  [15:0] ROM_In,
  input  Clk,
  input  Rst,
  output [7:0] ROM_Addr,
  output [31:0] RAM_Addr,
  output [31:0] R3,
  output [31:0] R7,
  output [31:0] RAM_Out,
  output [31:0] R2,
  output [31:0] R6,
  output [31:0] R1,
  output [31:0] R5,
  output [31:0] R0,
  output [31:0] R4,
  output Store
);

  wire Controller_1_p7, Controller_1_p9, Controller_1_p11, Controller_1_p12, Controller_1_p13,
       Controller_1_p16, Controller_1_p17;
  wire [3:0] Controller_1_p4, Controller_1_p10;
  wire [4:0] Controller_1_p15, multiplexer_3_out;
  wire [7:0] Controller_1_p14;
  wire [31:0] ALU_1_s, bit_extender_1_out, multiplexer_1_out, multiplexer_2_out, Regs_1_p15;

  // Controller Controller_1: pin names not known; wires that end beside it: ROM_In, Clk, Rst, Controller_1_p4, ROM_Addr, RAM_Addr, Controller_1_p7, Store, Controller_1_p9, Controller_1_p10, Controller_1_p11, Controller_1_p12, Controller_1_p13, Controller_1_p14, Controller_1_p15, Controller_1_p16, Controller_1_p17
  Multiplexer #(.width(32), .enable("false")) multiplexer_1 (
    .in0(ALU_1_s), .in1(RAM_In), .out(multiplexer_1_out), .sel(Controller_1_p7));
  // BancRegistre Regs_1: pin names not known; wires that end beside it: multiplexer_1_out, Controller_1_p11, Clk, R0, Rst, R1, R2, R3, R4, Controller_1_p12, R5, R6, Controller_1_p13, R7, Regs_1_p15, RAM_Out
  assign bit_extender_1_out = {{24{1'b0}}, Controller_1_p14};  // Bit_Extender bit_extender_1
  Multiplexer #(.width(32), .enable("false")) multiplexer_2 (
    .in0(RAM_Out), .in1(bit_extender_1_out), .out(multiplexer_2_out), .sel(Controller_1_p9));
  Multiplexer #(.width(5), .enable("false")) multiplexer_3 (
    .in0(multiplexer_2_out[4:0]), .in1(Controller_1_p15), .out(multiplexer_3_out), .sel(Controller_1_p16));
  ALU ALU_1 (
    .S(ALU_1_s), .Flags(Controller_1_p4), .Codop(Controller_1_p10), .CarryIn(Controller_1_p17),
    .A(multiplexer_2_out), .B(Regs_1_p15), .Shift(multiplexer_3_out));

  // Notes on the sheet:
  //   RAM/ALU Input selector
  //   Use data frpm Imm8 instead of A register
  //   Use data from register or immediate for shift
  //   Trigger carry for additionner
  //   Imm8 input for Move
endmodule
