// Logisim project Machine_Logisim3.circ as structural Verilog: 3 circuits, main circuit Facade
module Facade (
);

  wire and_1_out, and_2_out, and_3_out, and_4_out, and_5_out, and_6_out, BREAK, Clk, Clk_Button2,
       Clk_Button_out, clock_1_out, CONTINUE, CPU_1_pc_hold, d_ff_3_qn, d_ff_4_qn, decoder_1_out0,
       decoder_1_out1, decoder_1_out2, decoder_1_out3, decoder_1_out4, decoder_1_out5, decoder_2_out1,
       KEYB_Eof, KEYB_Read, KEYB_ReadEn, MMIO_En, or_1_out, or_2_out, RAM_En, Reset, RNG_Read,
       Rst_Button_out, RST_Signal, Store, Toggle, TTY_Upd;
  wire [1:0] comparator_1_eq;
  wire [3:0] binary_to_bcd_converter_1_p2, binary_to_bcd_converter_1_p3, binary_to_bcd_converter_1_p4,
       binary_to_bcd_converter_1_p5, CPU_1_flags;
  wire [4:0] JOY_X, JOY_Y;
  wire [6:0] KEYB_Char, TTY_Char;
  wire [15:0] bit_extender_1_out, bit_extender_3_out, multiplexer_3_out, register_7_q;
  wire [31:0] bcd8digits_1_bcd, CODE_Addr, CPU_1_r0, CPU_1_r1, CPU_1_r2, CPU_1_r3, CPU_1_r6, CPU_1_r7,
       CPU_1_sp, DATA_Addr, DATA_Out, Dip1, Dip2, Dip3, divider_1_out, divider_1_rem, MEM_Addr, MEM_Out,
       MMIO_Out, multiplier_1_out, R4, R5, RAM_Out, random_1_out, register_3_q, Res, ROM_Out, Screen;
  wire [31:1] undriven_2;
  wire [31:5] undriven_4, undriven_5;
  wire [31:7] undriven, undriven_3;

  DipSwitch dipswitch_1 (
    .sw1(Dip1[7]), .sw2(Dip1[6]), .sw3(Dip1[5]), .sw4(Dip1[4]), .sw5(Dip1[3]), .sw6(Dip1[2]), .sw7(Dip1[1]),
    .sw8(Dip1[0]));
  Multiplexer #(.width(32)) multiplexer_1 (.in0(CODE_Addr), .in1(DATA_Addr), .out(MEM_Addr), .sel(Toggle));
  RAM #(.addrWidth(16), .asyncread("true"), .dataWidth(32)) RAMa (
    .addr(bit_extender_1_out), .we(and_1_out), .oe(1'b1), .clk(Clk), .din(DATA_Out), .dout(RAM_Out));
  Bit_Extender #(.in_width(32), .\type ("zero")) bit_extender_1 (.in(MEM_Addr), .out(bit_extender_1_out));
  and and_1 (and_1_out, Store, RAM_En);
  // Probe on Dip1[7:0]
  DipSwitch dipswitch_2 (
    .sw1(Dip2[7]), .sw2(Dip2[6]), .sw3(Dip2[5]), .sw4(Dip2[4]), .sw5(Dip2[3]), .sw6(Dip2[2]), .sw7(Dip2[1]),
    .sw8(Dip2[0]));
  Keyboard keyboard_1 (.clk(Clk), .re(KEYB_Read), .clr(Reset), .avail(KEYB_Eof), .data(KEYB_Char));
  Decoder #(.select(4)) decoder_1 (
    .out0(decoder_1_out0), .out1(decoder_1_out1), .out2(decoder_1_out2), .out3(decoder_1_out3),
    .out4(decoder_1_out4), .out5(decoder_1_out5), .sel(MEM_Addr[3:0]), .en(and_2_out));  // open: out6, out7, out8, out9, out10, out11, out12, out13, out14, out15
  Comparator #(.width(16)) comparator_1 (.a(MEM_Addr[31:16]), .b({16{1'b0}}), .eq(comparator_1_eq[0]));  // open: gt, lt
  Comparator #(.width(28)) comparator_2 (.a(MEM_Addr[31:4]), .b({28{1'b1}}), .eq(comparator_1_eq[1]));  // open: gt, lt
  // Probe on Dip2[7:0]
  and and_2 (and_2_out, MMIO_En, Store);
  // Probe on MEM_Addr[3:0]
  Decoder #(.enable("false"), .select(2)) decoder_2 (
    .out0(RAM_En), .out1(decoder_2_out1), .out2(MMIO_En), .sel(comparator_1_eq));  // open: out3
  Multiplexer #(.select(2), .width(32)) multiplexer_2 (
    .in0(RAM_Out), .in1(ROM_Out), .in2(MMIO_Out), .out(MEM_Out), .sel(comparator_1_eq));  // open: in3
  // Probe on MEM_Out
  DipSwitch dipswitch_3 (
    .sw1(Dip3[7]), .sw2(Dip3[6]), .sw3(Dip3[5]), .sw4(Dip3[4]), .sw5(Dip3[3]), .sw6(Dip3[2]), .sw7(Dip3[1]),
    .sw8(Dip3[0]));
  // Probe on Dip3[7:0]
  Joystick #(.bits(5)) joystick_1 (.x(JOY_X), .y(JOY_Y));
  Register #(.trigger("falling"), .width(7)) register_1 (
    .D(DATA_Out[6:0]), .en(decoder_1_out0), .clk(Clk), .Q(TTY_Char), .clr(Reset));
  Register #(.width(32)) register_2 (.D(DATA_Out), .en(decoder_1_out1), .clk(Clk), .Q(Res), .clr(Reset));
  Register #(.width(32)) register_3 (.D(DATA_Out), .en(decoder_1_out2), .clk(Clk), .Q(register_3_q), .clr(Reset));
  Register #(.width(1)) register_4 (.D(DATA_Out[0]), .en(decoder_1_out4), .clk(Clk), .Q(RST_Signal), .clr(Reset));
  Register #(.width(1)) register_5 (.D(DATA_Out[0]), .en(decoder_1_out5), .clk(Clk), .Q(BREAK), .clr(or_1_out));
  or or_1 (or_1_out, Reset, CONTINUE);
  DotMatrix #(.inputtype("row"), .matrixcols(8), .matrixrows(4)) dotmatrix_1 (
    .row0(Screen[7:0]), .row1(Screen[15:8]), .row2(Screen[23:16]), .row3(Screen[31:24]));
  D_Flip_Flop d_ff_1 (.D(decoder_1_out0), .clk(Clk), .Q(TTY_Upd));  // open: Qn, preset, reset
  Register #(.width(32)) register_6 (.D(register_3_q), .en(and_3_out), .clk(Clk), .Q(Screen), .clr(Reset));
  and and_3 (and_3_out, DATA_Out[0], decoder_1_out3);
  // ROM #(.addrWidth(16), .dataWidth(16), .line("dual"), .misaligned("true")) ROMa: pin names not known; wires that end beside it: ROM_Out[15:0], ROM_Out[31:16]
  Bit_Extender #(.in_width(32), .\type ("zero")) bit_extender_2 (.in(MEM_Addr));  // open: out
  Clock clock_1 (.out(clock_1_out));
  and and_4 (and_4_out, clock_1_out, ~BREAK);  // AND_Gate
  Button Rst_Button (.out(Rst_Button_out));
  DotMatrix #(.inputtype("row"), .matrixcols(32), .matrixrows(1)) dotmatrix_2 (.row0(Res));
  Hex_Digit_Display hex_digit_display_1 (.value(Res[15:12]));  // open: dp
  Hex_Digit_Display hex_digit_display_2 (.value(Res[11:8]));  // open: dp
  D_Flip_Flop d_ff_2 (.D(KEYB_Read), .clk(Clk), .Q(KEYB_ReadEn), .reset(or_2_out));  // open: Qn, preset
  or or_2 (or_2_out, ~KEYB_Read, Reset);  // OR_Gate
  or or_3 (Clk, and_4_out, Clk_Button_out, Clk_Button2);
  Button Clk_Button (.out(Clk_Button_out));
  Bit_Extender #(.in_width(32), .\type ("zero")) bit_extender_3 (.in(MEM_Out), .out(bit_extender_3_out));
  Hex_Digit_Display hex_digit_display_3 (.value(Res[7:4]));  // open: dp
  Hex_Digit_Display hex_digit_display_4 (.value(Res[3:0]));  // open: dp
  or or_4 (Reset, Rst_Button_out, RST_Signal);
  Register #(.width(16)) register_7 (.D(bit_extender_3_out), .en(d_ff_3_qn), .clk(Clk), .Q(register_7_q));  // open: clr
  D_Flip_Flop #(.trigger("falling")) d_ff_3 (
    .D(CPU_1_pc_hold), .clk(Clk), .Q(Toggle), .Qn(d_ff_3_qn));  // open: preset, reset
  // Probe on ROM_Out
  Button button_1 (.out(CONTINUE));
  // Binary_to_BCD_converter #(.binvalue(13)) binary_to_bcd_converter_1: pin names not known; wires that end beside it: Res[12:0], binary_to_bcd_converter_1_p2, binary_to_bcd_converter_1_p3, binary_to_bcd_converter_1_p4, binary_to_bcd_converter_1_p5
  D_Flip_Flop #(.trigger("falling")) d_ff_4 (.D(1'b0), .clk(Clk), .Qn(d_ff_4_qn), .preset(Reset));  // open: Q, reset
  Button button_2 (.out(Clk_Button2));
  // Probe on Res
  Hex_Digit_Display hex_digit_display_5 (.value(binary_to_bcd_converter_1_p3));  // open: dp
  Hex_Digit_Display hex_digit_display_6 (.value(binary_to_bcd_converter_1_p2));  // open: dp
  Random #(.width(32)) random_1 (.next(RNG_Read), .clk(Clk), .out(random_1_out));  // open: clr
  and and_5 (and_5_out, Clk, d_ff_4_qn);
  Multiplexer #(.width(16)) multiplexer_3 (
    .in0(bit_extender_3_out), .in1(register_7_q), .out(multiplexer_3_out), .sel(Toggle));
  // Probe on multiplexer_3_out
  Hex_Digit_Display hex_digit_display_7 (.value(binary_to_bcd_converter_1_p4));  // open: dp
  Hex_Digit_Display hex_digit_display_8 (.value(binary_to_bcd_converter_1_p5));  // open: dp
  BCD8digits bcd8digits_1 (.BCD(bcd8digits_1_bcd), .Number(Res));
  Divider #(.width(32)) divider_1 (.a(R4), .b(R5), .out(divider_1_out), .rem(divider_1_rem));  // open: upper
  // Probe on CPU_1_r3
  // Probe on CPU_1_r2
  // Probe on CPU_1_r1
  // Probe on CPU_1_r0
  TTY tty_1 (.data(TTY_Char), .clk(Clk), .we(TTY_Upd), .clr(Reset));
  // Probe on CPU_1_r7
  // Probe on CPU_1_r6
  // Probe on R5
  // Probe on R4
  Multiplexer #(.select(4), .width(32)) multiplexer_4 (
    .in0({undriven, TTY_Char}), .in1(Res), .in2(register_3_q), .in3(Dip1), .in4(Dip2), .in5(Dip3),
    .in6({undriven_2, KEYB_Eof}), .in7({undriven_3, KEYB_Char}), .in8({undriven_5, JOY_X}),
    .in9({undriven_4, JOY_Y}), .in10(random_1_out), .in11(bcd8digits_1_bcd), .in12(divider_1_out),
    .in13(divider_1_rem), .out(MMIO_Out), .sel(MEM_Addr[3:0]));  // open: in14, in15
  // Probe on CPU_1_flags
  CPU CPU_1 (
    .Flags(CPU_1_flags), .SP(CPU_1_sp), .RAM_Out(DATA_Out), .PC_Hold(CPU_1_pc_hold), .ROM_Addr(CODE_Addr),
    .Store(Store), .RAM_Addr(DATA_Addr), .R0(CPU_1_r0), .R1(CPU_1_r1), .R2(CPU_1_r2), .R3(CPU_1_r3), .R4(R4),
    .R5(R5), .R6(CPU_1_r6), .R7(CPU_1_r7), .RAM_In(MEM_Out), .ROM_In(multiplexer_3_out), .Clk(and_5_out),
    .Reset(Reset));
  Bit_Extender #(.in_width(32), .\type ("zero")) bit_extender_4 ();  // open: in, out
  and and_6 (and_6_out, ~Store, MMIO_En);  // AND_Gate
  Decoder #(.select(4)) decoder_3 (
    .out7(KEYB_Read), .out10(RNG_Read), .sel(MEM_Addr[3:0]), .en(and_6_out));  // open: out0, out1, out2, out3, out4, out5, out6, out8, out9, out11, out12, out13, out14, out15
  Pull_Resistor pull_resistor_1 (.node(MMIO_Out));
  // Probe on DATA_Addr
  // Probe on DATA_Out
  // Probe on CPU_1_sp
  // Probe on multiplier_1_out
  Multiplier #(.width(32)) multiplier_1 (.a(32'h2), .b(CODE_Addr), .out(multiplier_1_out));  // open: cin, cout

  // Other names for the same wires on the sheet: MMIO_Addr[3:0] = MEM_Addr[3:0]

  // Notes on the sheet:
  //   Entrées / Sorties mappées en mémoire
  //   Sorties
  //   contents of ROMa (hex, n*v repeats v):
  //   e7fe af00 b0ff b0ff b082 f037 119 b081 b081 9400 b081 9500 b081 9700 af02 220f 43d1 2304 43dc 6823
  //   2b00 d01d 2800 d006 200e 43c0 6803 252d 600d 425b 6003 6823 4618 71c 91b 2c00 d0f9 e003 903 4010
  //   3030 6008 4618 2800 d1f7 9f00 b001 9d00 b001 9c00 b001 b001 4770 2030 6008 9f00 b001 9d00 b001 9c00
  //   b001 b001 4770 b081 b081 9700 af00 b088 200f 43c1 2041 6008 203d 9105 9003 6008 2009 43c6 2008 43c0
  //   9007 2400 6830 2800 d0fb 9807 6800 601 e09 290a d00b 460a 3a30 2a09 d8f1 9a05 6011 210a 4361 30d0
  //   600 e00 1844 e7e8 200a 9905 9004 6008 2042 6008 9803 6008 2500 6830 2800 d0fb 9807 6800 601 e09 290a
  //   d00b 460a 3a30 2a09 d8f1 9a05 6011 9904 434d 30d0 600 e00 1945 e7e8 9905 9804 6008 202b 6008 202d
  //   6008 202a 6008 1928 9006 1b60 9002 4620 4368 9001 6830 2800 d0fb 9807 6800 600 e00 382a 2805 d8f4 80
  //   a101 5809 9806 468f 133 0 143 0 131 0 137 0 131 0 13b 0 e7e2 9801 e004 9802 e002 26 2003 43c0 6800
  //   210e 43c9 6008 9905 9804 6008 2052 6008 9803 6008 2000 f73e 6830 2800 d0fb 200b 43c0 2101 6001 e7c6
  //   Reprendre après un point d'arrêt
  //   Tic d'horloge
  //   Entrées
  //   PC effectif
endmodule

module CPU (
  input  [31:0] RAM_In,
  input  [15:0] ROM_In,
  input  Clk,
  input  Reset,
  output [31:0] R3,
  output [31:0] R7,
  output [31:0] R2,
  output [31:0] R6,
  output [31:0] R1,
  output [31:0] R5,
  output [31:0] R0,
  output [31:0] R4,
  output [31:0] RAM_Out,
  output [31:0] ROM_Addr,
  output [31:0] RAM_Addr,
  output Store,
  output [3:0] Flags,
  output [31:0] SP,
  output PC_Hold
);

  wire Controller_1_p16, Controller_1_p18, Controller_1_p20, Controller_1_p21, Controller_1_p22,
       Controller_1_p25, Controller_1_p26;
  wire [3:0] Controller_1_p4, Controller_1_p19;
  wire [4:0] Controller_1_p24, multiplexer_3_out;
  wire [31:0] ALU_1_s, Controller_1_p23, multiplexer_1_out, multiplexer_2_out, Regs_1_p15, Regs_1_p16;

  Multiplexer #(.width(32)) multiplexer_1 (
    .in0(ALU_1_s), .in1(RAM_In), .out(multiplexer_1_out), .sel(Controller_1_p16));
  // Controller Controller_1: pin names not known; wires that end beside it: ROM_In, Clk, Reset, Controller_1_p4, R0, R1, R2, R3, R4, R5, R6, R7, RAM_In, ROM_Addr, RAM_Addr, Controller_1_p16, Store, Controller_1_p18, Controller_1_p19, Controller_1_p20, Controller_1_p21, Controller_1_p22, Controller_1_p23, Controller_1_p24, Controller_1_p25, Controller_1_p26, Flags, SP, PC_Hold
  // BancRegistre Regs_1: pin names not known; wires that end beside it: multiplexer_1_out, Controller_1_p20, Clk, R0, Reset, R1, R2, R3, R4, Controller_1_p21, R5, R6, Controller_1_p22, R7, Regs_1_p15, Regs_1_p16
  Multiplexer #(.width(32)) multiplexer_2 (
    .in0(Regs_1_p16), .in1(Controller_1_p23), .out(multiplexer_2_out), .sel(Controller_1_p18));
  Multiplexer #(.width(5)) multiplexer_3 (
    .in0(Regs_1_p16[4:0]), .in1(Controller_1_p24), .out(multiplexer_3_out), .sel(Controller_1_p25));
  ALU ALU_1 (
    .S(ALU_1_s), .Flags(Controller_1_p4), .Codop(Controller_1_p19), .CarryIn(Controller_1_p26),
    .A(multiplexer_2_out), .B(Regs_1_p15), .Shift(multiplexer_3_out));
  Multiplexer #(.width(32)) multiplexer_4 (.in0(Regs_1_p16), .in1(Controller_1_p23), .out(RAM_Out), .sel(Store));
endmodule

module BCD8digits (
  input  [31:0] Number,
  output [31:0] BCD
);

  wire [31:0] divider_1_out, divider_2_out, divider_3_out, divider_4_out, divider_5_out, divider_6_out,
       divider_7_out;
  wire [31:4] divider_1_rem, divider_2_rem, divider_3_rem, divider_4_rem, divider_5_rem, divider_6_rem,
       divider_7_rem, divider_8_rem;

  Divider #(.width(32)) divider_1 (
    .a(Number), .b(32'ha), .out(divider_1_out), .rem({divider_1_rem, BCD[31:28]}));  // open: upper
  Divider #(.width(32)) divider_2 (
    .a(divider_1_out), .b(32'ha), .out(divider_2_out), .rem({divider_2_rem, BCD[27:24]}));  // open: upper
  Divider #(.width(32)) divider_3 (
    .a(divider_2_out), .b(32'ha), .out(divider_3_out), .rem({divider_3_rem, BCD[23:20]}));  // open: upper
  Divider #(.width(32)) divider_4 (
    .a(divider_3_out), .b(32'ha), .out(divider_4_out), .rem({divider_4_rem, BCD[19:16]}));  // open: upper
  Divider #(.width(32)) divider_5 (
    .a(divider_4_out), .b(32'ha), .out(divider_5_out), .rem({divider_5_rem, BCD[15:12]}));  // open: upper
  Divider #(.width(32)) divider_6 (
    .a(divider_5_out), .b(32'ha), .out(divider_6_out), .rem({divider_6_rem, BCD[11:8]}));  // open: upper
  Divider #(.width(32)) divider_7 (
    .a(divider_6_out), .b(32'ha), .out(divider_7_out), .rem({divider_7_rem, BCD[7:4]}));  // open: upper
  Divider #(.width(32)) divider_8 (.a(divider_7_out), .b(32'ha), .rem({divider_8_rem, BCD[3:0]}));  // open: out, upper
  // Probe on BCD
endmodule
